// Digital circuit main.dig as structural Verilog
module main (
  input  clk,
  input  in_2,
  output IP_plus__plus,
  output [1:0] TO,
  output source,
  output A
);

  wire fetch, RESET, ToRAM;
  wire [1:0] micro_step;
  wire [3:0] micro_addr;
  wire [7:0] data, RAM_D, RF_s, TMP;
  wire [9:0] ADDR;
  wire [15:0] AX, BX, CX, DX, R_addr;

  ROM #(.AddrBits(10), .Bits(8)) PRG (.A(ADDR), .sel(in_2), .D(data));
  Button button_1 (.out(RESET));
  sequenser #(.applicationType("IVERILOG")) u_sequenser (
    .RESET(RESET), .clk(clk), .aseq(micro_addr), .iseq({A, source, TO, IP_plus__plus}), .fetch(fetch),
    .count(micro_step));
  CPU #(.applicationType("IVERILOG")) u_CPU (
    .RESET(RESET), .clk(clk), .iseq({A, source, TO, IP_plus__plus}), .fetch(fetch), .DATAB(data), .IP(ADDR),
    .OP(micro_addr), .AX(AX), .CX(CX), .DX(DX), .BX(BX), .TMP(TMP), .Raddr(R_addr), .RFsrc(RF_s),
    .toRAM(ToRAM));
  BlockRAMDualPort #(.AddrBits(16), .Bits(8)) blockramdualport_1 (
    .A(R_addr), .Din(RF_s), .str(ToRAM), .C(clk), .D(RAM_D));

  // Other names for the same wires on the sheet: iseq[4:0] = {A, source, TO, IP_plus__plus}

  // Notes on the sheet:
  //   in_2: default 1
  //   contents of PRG (hex, n*v repeats v):
  //   b0,aa,a2,30,0,b0,55,a2,31,0,b3,40,88,7
endmodule

/* Code of sequenser:
`define FETCH_BIT 5

module sequenser(
  input  RESET,
  input  clk,
  input  [3:0]aseq, 
  output [`FETCH_BIT-1:0]iseq,
  output fetch,
  output reg [1:0]count = 2'd0
);

reg [`FETCH_BIT:0]sequence[63:0];

always@(posedge clk or posedge RESET) begin
  if(RESET) begin
     count <= 2'd0;
//TO:   toTMP = 2'b01, toRAM = 2'b10, toRF = 2'b11;
//R:    AL = 0, reg = 1
//A:    TMP = 0, TMP.reg = 1
/* start                             F A R TO IP    * /
     sequence[{2'b00, 4'b0000}] = 6'b1_0_0_00_1;
// 100010.d.w mod.reg.r/m op=100010 d=1, w=0  (88 07) MOV [BX], AL 100010.0.0 00.000.111 reg -> r/m r/m=[BX}
     sequence[{2'b00, 4'b1000}] = 6'b0_0_0_01_1;   
     sequence[{2'b01, 4'b1000}] = 6'b1_1_0_10_1;
     sequence[{2'b10, 4'b1000}] = 6'b0_0_0_00_0;
     sequence[{2'b11, 4'b1000}] = 6'b0_0_0_00_0;
// 1011.0.reg  op=1011 d=0 --> op.d.reg #const8 (B0 AA)  MOV AL, 0xAA
/*                                   F A R TO IP    * /
     sequence[{2'b00, 4'b1011}] = 6'b0_0_0_11_1;   
     sequence[{2'b01, 4'b1011}] = 6'b1_0_0_00_1;
     sequence[{2'b10, 4'b1011}] = 6'b0_0_0_00_0;
     sequence[{2'b11, 4'b1011}] = 6'b0_0_0_00_0;
// 1010.00.1.w addr_l addr_h d=1 w=0 -> A2 00 30  MOV byte ptr [addr], AL
/*                                   F A R TO IP    * /
     sequence[{2'b00, 4'b1010}] = 6'b0_0_0_01_1;
     sequence[{2'b01, 4'b1010}] = 6'b0_0_0_10_1;   // R=0 => source A, A=0 => addr TMP
     sequence[{2'b10, 4'b1010}] = 6'b1_0_0_00_1;   
     sequence[{2'b11, 4'b1010}] = 6'b0_0_0_00_0;
  end else begin
     count <= (fetch)? 2'd0 : (count + 1'b1);
  end
end

assign iseq = sequence[{count, aseq}][(`FETCH_BIT-1):0];
assign fetch = sequence[{count, aseq}][`FETCH_BIT];
endmodule
*/

/* Code of CPU:
module CPU(
  input  RESET,
  input  clk,
  input  [4:0]iseq,
  input  fetch,
  input  [7:0]DATAB,
  output reg [9:0]IP,
  output [3:0]OP,
  output [15:0]AX,
  output [15:0]CX,
  output [15:0]DX,
  output [15:0]BX,
  output [7:0]TMP,
  output [15:0]Raddr,
  output [7:0]RFsrc,
  output toRAM
);

reg [7:0]RF[7:0];
reg [7:0]OP_CODE;
reg [7:0]RgTMP;

wire A, source, INC_IP;
wire [1:0]target;
wire [2:0]rg;
wire d;

assign {OP,d,rg} = OP_CODE;
assign {A, source, target, INC_IP} = iseq;

wire    toRF = (target == 2'b11);
wire   toTMP = (target == 2'b01);
assign toRAM = (target == 2'b10);

wire [2:0]src = (source)? rg : 3'b000;

always@(posedge clk or posedge RESET) begin
  if(RESET) begin
     IP <= 10'd0;
     OP_CODE <= 8'd0;
  end else begin
     if(fetch) OP_CODE <= DATAB[7:0];
     IP <= IP + INC_IP;
     if(toRF) RF[rg] <= DATAB[7:0];
     if(toTMP) RgTMP[7:0] <= DATAB;
  end
end
assign AX = {RF[4], RF[0]};
assign CX = {RF[5], RF[1]};
assign DX = {RF[6], RF[2]};
assign BX = {RF[7], RF[3]};
assign RFsrc = RF[src];

wire [15:0]MuxAddr = 
 (RgTMP == 3'd7)? BX :
 (RgTMP == 3'd6)? AX : 
 (RgTMP == 3'd5)? CX : 
 (RgTMP == 3'd4)? DX : 
 (RgTMP == 3'd3)? AX : 
 (RgTMP == 3'd2)? AX : 
 (RgTMP == 3'd1)? AX : AX;

assign Raddr = (A)? MuxAddr : {DATAB[7:0], RgTMP};
assign TMP = RgTMP;
endmodule
*/
